// Logisim project PAC20131.circ as structural Verilog: 19 circuits, main circuit Banco de Registradores
module Banco_de_Registradores (
  input  [15:0] Entrada_de_Dados,
  input  [3:0] Sinais_de_Controle,
  input  [15:0] \Endereço ,
  output [15:0] \Saiída 
);

  wire [15:0] \A_saída , \B_saída , \C_saída , \D_saída ;
  wire [18:0] demultiplexer_1_out0, demultiplexer_1_out1, demultiplexer_1_out2, demultiplexer_1_out3;

  Demultiplexer #(.select(2), .width(19), .tristate("true")) demultiplexer_1 (
    .out0(demultiplexer_1_out0), .out1(demultiplexer_1_out1), .out2(demultiplexer_1_out2),
    .out3(demultiplexer_1_out3), .in({Sinais_de_Controle[2:0], Entrada_de_Dados}), .sel(\Endereço [1:0]),
    .en(Sinais_de_Controle[3]));
  Registrador A (
    .Entrada(demultiplexer_1_out0[15:0]), .\Saída (\A_saída ),
    .Sinais_de_Controle(demultiplexer_1_out0[18:16]));
  Registrador B (
    .Entrada(demultiplexer_1_out1[15:0]), .\Saída (\B_saída ),
    .Sinais_de_Controle(demultiplexer_1_out1[18:16]));
  Multiplexer #(.select(2), .width(16)) multiplexer_1 (
    .in0(\A_saída ), .in1(\B_saída ), .in2(\C_saída ), .in3(\D_saída ), .out(\Saiída ),
    .sel(\Endereço [1:0]), .en(Sinais_de_Controle[3]));
  Registrador C (
    .Entrada(demultiplexer_1_out2[15:0]), .\Saída (\C_saída ),
    .Sinais_de_Controle(demultiplexer_1_out2[18:16]));
  Registrador D (
    .Entrada(demultiplexer_1_out3[15:0]), .\Saída (\D_saída ),
    .Sinais_de_Controle(demultiplexer_1_out3[18:16]));

  // Notes on the sheet:
  //   Bit      Função
  //   0         1 - Habilitar ; 0 Desabilitar
  //   1-2        Sinais de Controle do Registrador
  //     4         Clock do Circuito
  //   fffc                   00                   Reg A
  //   fffd                   01                   Reg B
  //   fffe                   10                   Reg C
  //   ffff                    11                   Reg D
  //   Endereço   Correspondência   Registrador
endmodule

module Registrador (
  input  [2:0] Sinais_de_Controle,
  input  [15:0] Entrada,
  output [15:0] \Saída 
);

  wire and_1_out, Clear, Habilitar, Modo_R_W, not_1_out;
  wire [15:0] controlled_buffer_1_out, Registrador_q;

  Multiplexer #(.select(2), .width(3), .enable("false")) multiplexer_1 (
    .in0(3'b000), .in1(3'b001), .in2(3'b101), .in3(3'b011), .out({Modo_R_W, Clear, Habilitar}),
    .sel(Sinais_de_Controle[2:1]));
  assign controlled_buffer_1_out = Modo_R_W ? Entrada : 16'bz;  // Controlled_Buffer controlled_buffer_1
  not not_1 (not_1_out, Modo_R_W);
  assign \Saída  = and_1_out ? Registrador_q : 16'bz;  // Controlled_Buffer controlled_buffer_2
  Register #(.width(16)) Registrador (
    .D(controlled_buffer_1_out), .en(Habilitar), .Q(Registrador_q), .clk(Sinais_de_Controle[0]), .clr(Clear));
  and and_1 (and_1_out, Habilitar, not_1_out);

  // Other names for the same wires on the sheet: Clock = Sinais_de_Controle[0]

  // Notes on the sheet:
  //   00 - Registrador Desabilitado
  //   01 - Modo de Leitura
  //   10 - Modo de Escrita
  //   11 - Clear
  //   Habilitar
  //   0
  //   0
  //   0
  //   0
  //   1
  //   1
  //   1
  //   1
  //   Clear
  //   Modo R/W
  //   0
  //   0
  //   0
  //   1
  //   1
  //   1
  //   0
  //   0
  //   1
  //   0
  //   0
  //   1
  //   1
  //   1
  //   0
  //   1
  //   F(x)
  //   1
  //   Registrador Desabilitado
  //   x
  //   x
  //   x
  //   Modo de Leitura
  //   1
  //   Modo de Escrita
  //   1
  //   1
  //   Clear
  //   x
endmodule

module Contador_de_Programa__PC (
  input  [2:0] Sinais_de_Controle,
  input  [15:0] Entrada,
  output [15:0] \Saída 
);

  wire Carregar, Habilitar, Reset;

  Multiplexer #(.select(2), .width(3), .disabled(0), .enable("false")) multiplexer_1 (
    .in0(3'b000), .in1(3'b001), .in2(3'b100), .in3(3'b011), .out({Carregar, Reset, Habilitar}),
    .sel(Sinais_de_Controle[2:1]));
  Counter #(.width(16), .max('hffff), .ongoal("stay")) counter_1 (
    .load(Carregar), .D(Entrada), .count(Habilitar), .Q(\Saída ), .clk(Sinais_de_Controle[0]), .clr(Reset));  // open: carry

  // Other names for the same wires on the sheet: Clock = Sinais_de_Controle[0]

  // Notes on the sheet:
  //   00 - Para o contador
  //   01 - Conta
  //   10 - Carrega valor na entrada
  //   11 - Reset
  //   Habilitar
  //   0
  //   0
  //   0
  //   0
  //   1
  //   1
  //   1
  //   1
  //   Modo R/W
  //   Clear
  //   0
  //   0
  //   0
  //   1
  //   1
  //   1
  //   0
  //   0
  //   1
  //   0
  //   0
  //   1
  //   1
  //   1
  //   0
  //   1
  //   F(x)
  //   1
  //   Registrador Desabilitado
  //   x
  //   x
  //   x
  //   Modo de Leitura
  //   1
  //   Modo de Escrita
  //   1
  //   1
  //   Clear
  //   x
endmodule

module Registrador_de_Flags__RF (
  input  [1:0] Sinais_de_Controle,
  input  [3:0] Entrada,
  output [15:0] \Saída 
);

  wire Clear, Habilitar, Modo_R_W, not_1_out;
  wire [3:0] controlled_buffer_1_out, Registrador_q;

  Multiplexer #(.width(3), .enable("false")) multiplexer_1 (
    .in0(3'b001), .in1(3'b101), .out({Modo_R_W, Clear, Habilitar}), .sel(Sinais_de_Controle[1]));
  assign controlled_buffer_1_out = Modo_R_W ? Entrada : 4'bz;  // Controlled_Buffer controlled_buffer_1
  assign \Saída [3:0] = not_1_out ? Registrador_q : 4'bz;  // Controlled_Buffer controlled_buffer_2
  Register #(.width(4)) Registrador (
    .D(controlled_buffer_1_out), .en(Habilitar), .Q(Registrador_q), .clk(Sinais_de_Controle[0]), .clr(Clear));
  not not_1 (not_1_out, Modo_R_W);

  assign \Saída [15:4] = {12{1'b0}};

  // Other names for the same wires on the sheet: Clock = Sinais_de_Controle[0]

  // Notes on the sheet:
  //   0 - Modo de Leitura
  //   1 - Modo de Escrita
  //   Habilitar
  //   0
  //   0
  //   0
  //   0
  //   1
  //   1
  //   1
  //   1
  //   Clear
  //   0
  //   0
  //   1
  //   1
  //   0
  //   0
  //   1
  //   1
  //   Modo R/W
  //   0
  //   1
  //   0
  //   1
  //   0
  //   1
  //   0
  //   1
  //   F(x)
  //   x
  //   x
  //   x
  //   x
  //   Modo de Leitura
  //   1
  //   Modo de Escrita
  //   1
  //   x
  //   x
endmodule

module Registrador_da_ULA (
  input  [1:0] Sinais_de_Controle,
  input  [15:0] Entrada,
  output [15:0] \Saída 
);

  wire Clear, Habilitar, Modo_R_W, not_1_out;
  wire [15:0] controlled_buffer_1_out, Registrador_q;

  Multiplexer #(.width(3), .enable("false")) multiplexer_1 (
    .in0(3'b001), .in1(3'b101), .out({Modo_R_W, Clear, Habilitar}), .sel(Sinais_de_Controle[1]));
  assign controlled_buffer_1_out = Modo_R_W ? Entrada : 16'bz;  // Controlled_Buffer controlled_buffer_1
  Register #(.width(16)) Registrador (
    .D(controlled_buffer_1_out), .en(Habilitar), .Q(Registrador_q), .clk(Sinais_de_Controle[0]), .clr(Clear));
  not not_1 (not_1_out, Modo_R_W);
  assign \Saída  = not_1_out ? Registrador_q : 16'bz;  // Controlled_Buffer controlled_buffer_2

  // Other names for the same wires on the sheet: Clock = Sinais_de_Controle[0]

  // Notes on the sheet:
  //   0 - Modo de Leitura
  //   1 - Modo de Escrita
  //   Habilitar
  //   0
  //   0
  //   0
  //   0
  //   1
  //   1
  //   1
  //   1
  //   Clear
  //   0
  //   0
  //   1
  //   1
  //   0
  //   0
  //   1
  //   1
  //   Modo R/W
  //   0
  //   1
  //   0
  //   1
  //   0
  //   1
  //   0
  //   1
  //   F(x)
  //   x
  //   x
  //   x
  //   x
  //   Modo de Leitura
  //   1
  //   Modo de Escrita
  //   1
  //   x
  //   x
endmodule

module Unidade_de_Deslocamento (
  input  [15:0] Entrada,
  input  [7:0] Sinais_de_Controle,
  output [15:0] \Saída 
);

  wire not_1_out, not_2_out;
  wire [15:0] controlled_buffer_1_out, multiplexer_1_out, Registrador_2_q, Registrador_q, shifter_1_out,
       shifter_2_out, shifter_3_out, shifter_4_out;
  wire [19:0] demultiplexer_1_out0, demultiplexer_1_out1, demultiplexer_1_out2, demultiplexer_1_out3;

  assign controlled_buffer_1_out = not_1_out ? Entrada : 16'bz;  // Controlled_Buffer controlled_buffer_1
  Register #(.width(16)) Registrador (
    .D(controlled_buffer_1_out), .en(not_1_out), .Q(Registrador_q), .clk(Sinais_de_Controle[7]));  // open: clr
  Demultiplexer #(.select(2), .width(20)) demultiplexer_1 (
    .out0(demultiplexer_1_out0), .out1(demultiplexer_1_out1), .out2(demultiplexer_1_out2),
    .out3(demultiplexer_1_out3), .in({Sinais_de_Controle[6:3], Registrador_q}),
    .sel(Sinais_de_Controle[2:1]), .en(not_1_out));
  not not_1 (not_1_out, Sinais_de_Controle[0]);
  Shifter #(.width(16)) shifter_1 (
    .in(demultiplexer_1_out0[15:0]), .\dist (demultiplexer_1_out0[19:16]), .out(shifter_1_out));
  Shifter #(.width(16), .shift("lr")) shifter_2 (
    .in(demultiplexer_1_out1[15:0]), .\dist (demultiplexer_1_out1[19:16]), .out(shifter_2_out));
  Shifter #(.width(16), .shift("rl")) shifter_3 (
    .in(demultiplexer_1_out2[15:0]), .\dist (demultiplexer_1_out2[19:16]), .out(shifter_3_out));
  Shifter #(.width(16), .shift("rr")) shifter_4 (
    .in(demultiplexer_1_out3[15:0]), .\dist (demultiplexer_1_out3[19:16]), .out(shifter_4_out));
  Multiplexer #(.select(2), .width(16)) multiplexer_1 (
    .in0(shifter_1_out), .in1(shifter_2_out), .in2(shifter_3_out), .in3(shifter_4_out),
    .out(multiplexer_1_out), .sel(Sinais_de_Controle[2:1]), .en(not_2_out));
  not not_2 (not_2_out, Sinais_de_Controle[0]);
  assign \Saída  = Sinais_de_Controle[0] ? Registrador_2_q : 16'bz;  // Controlled_Buffer controlled_buffer_2
  Register #(.width(16)) Registrador_2 (
    .D(multiplexer_1_out), .en(not_2_out), .Q(Registrador_2_q), .clk(Sinais_de_Controle[7]));  // open: clr

  // Other names for the same wires on the sheet: Clock = Sinais_de_Controle[7]

  // Notes on the sheet:
  //   Bit       Função
  //   0       0 - Entrada de Dados ; 1 - Saída de Dados
  //   1,2      Operação
  //   3-6      Número de vezes
  //   7       Clock do Circuito
endmodule

module Unidade_de_Salto (
  input  [3:0] in_1
);

  wire [15:0] \registrador_de_flags_rf_1_saída ;

  Registrador_de_Flags__RF registrador_de_flags_rf_1 (
    .Entrada(in_1), .\Saída (\registrador_de_flags_rf_1_saída ));  // open: Sinais_de_Controle
  // OR_Gate or has open pins: in0=\registrador_de_flags_rf_1_saída [0], in1=\registrador_de_flags_rf_1_saída [2], out=open
  // OR_Gate or_2 has open pins: in0=\registrador_de_flags_rf_1_saída [1], in1=\registrador_de_flags_rf_1_saída [2], out=open
endmodule

module Direcionador (
  input  [15:0] Entrada_A,
  input  Direcionador,
  input  [15:0] Entrada_B,
  output [15:0] \Saída_A ,
  output [15:0] \Saída_B 
);

  wire not_1_out;

  assign \Saída_A  = not_1_out ? Entrada_A : 16'bz;  // Controlled_Buffer controlled_buffer_1
  not not_1 (not_1_out, Direcionador);
  assign \Saída_B  = Direcionador ? Entrada_B : 16'bz;  // Controlled_Buffer controlled_buffer_2
endmodule

module Operacoes (
  input  [15:0] Operando_A,
  input  [15:0] Operando_B,
  input  [3:0] Sinais_de_Controle,
  output [15:0] Resultado,
  output [3:0] Flags
);

  wire and_2_out, Flag_de_Overflow, Flag_de_Resultado_Negativo, Igual, Maior, Menor, not_2_out;
  wire [15:0] AND, AND_A, AND_B, Carry_Out, \Comparação_A , \Comparação_B , Dividendo_A, Dividendo_B,
       \Divisão , Multiplicando_A, Multiplicando_B, \Multiplicação , Negando, \Negação , OR, OR_A, OR_B,
       Resto, Soma, Soma_A, Soma_B, \Subtração , \Subtração_A , \Subtração_B , XOR, XOR_A, XOR_B;

  Demultiplexer #(.select(4), .width(16), .tristate("true"), .enable("false")) demultiplexer_1 (
    .out0(Soma_A), .out1(\Subtração_A ), .out2(Multiplicando_A), .out3(Dividendo_A), .out4(AND_A),
    .out5(OR_A), .out6(XOR_A), .out7(\Comparação_A ), .out8(Negando), .in(Operando_A),
    .sel(Sinais_de_Controle));  // open: out9, out10, out11, out12, out13, out14, out15
  Demultiplexer #(.select(4), .width(16), .tristate("true"), .enable("false")) demultiplexer_2 (
    .out0(Soma_B), .out1(\Subtração_B ), .out2(Multiplicando_B), .out3(Dividendo_B), .out4(AND_B),
    .out5(OR_B), .out6(XOR_B), .out7(\Comparação_B ), .in(Operando_B), .sel(Sinais_de_Controle));  // open: out8, out9, out10, out11, out12, out13, out14, out15
  Adder #(.width(16)) adder_1 (.a(Soma_A), .b(Soma_B), .out(Soma), .cout(Flag_de_Overflow));  // open: cin
  Subtractor #(.width(16)) subtractor_1 (
    .a(\Subtração_A ), .b(\Subtração_B ), .out(\Subtração ), .bout(Flag_de_Resultado_Negativo));  // open: bin
  Multiplier #(.width(16)) multiplier_1 (
    .a(Multiplicando_A), .b(Multiplicando_B), .out(\Multiplicação ), .cout(Carry_Out));  // open: cin
  Divider #(.width(16)) divider_1 (.a(Dividendo_A), .b(Dividendo_B), .out(\Divisão ), .rem(Resto));  // open: upper
  Comparator #(.width(16)) comparator_1 (.a(\Comparação_A ), .b(\Comparação_B ), .gt(Maior), .eq(Igual), .lt(Menor));
  assign AND = AND_A & AND_B;  // AND_Gate and_1, 16 bits wide
  assign OR = OR_A | OR_B;  // OR_Gate or_1, 16 bits wide
  assign XOR = XOR_A ^ XOR_B;  // XOR_Gate xor_1, 16 bits wide
  assign \Negação  = ~Negando;  // NOT_Gate not_1, 16 bits wide
  and and_2 (and_2_out, Sinais_de_Controle[0], Sinais_de_Controle[1], Sinais_de_Controle[2], ~Sinais_de_Controle[3]);  // AND_Gate
  not not_2 (not_2_out, and_2_out);
  Multiplexer #(.select(4), .width(16), .disabled(0), .enable("false")) multiplexer_1 (
    .in0(Soma), .in1(\Subtração ), .in2(\Multiplicação ), .in3(\Divisão ), .in4(AND), .in5(OR), .in6(XOR),
    .in8(\Negação ), .out(Resultado), .sel(Sinais_de_Controle));  // open: in7, in9, in10, in11, in12, in13, in14, in15
  Seletor_de_Flags seletor_de_flags_1 (
    .Negativo(Flag_de_Resultado_Negativo), .\Operação (Sinais_de_Controle), .Overflow(Flag_de_Overflow),
    .Flag(Flags[0]));
  assign Flags[3:1] = and_2_out ? {Igual, Maior, Menor} : 3'bz;  // Controlled_Buffer controlled_buffer_1
  assign Flags[3:1] = not_2_out ? 3'b000 : 3'bz;  // Controlled_Buffer controlled_buffer_2

  // Other names for the same wires on the sheet: Operação[3:0] = Sinais_de_Controle

  // Notes on the sheet:
  //   Resultado: pull=up
endmodule

module Seletor_de_Flags (
  input  Negativo,
  input  [3:0] \Operação ,
  input  Overflow,
  output Flag
);

  wire and_1_out, and_2_out, controlled_buffer_1_out, controlled_buffer_3_out, not_1_out, not_2_out;

  and and_1 (and_1_out, \Operação [0], ~\Operação [1], ~\Operação [2], ~\Operação [3]);  // AND_Gate
  and and_2 (and_2_out, ~\Operação [0], ~\Operação [1], ~\Operação [2], ~\Operação [3]);  // AND_Gate
  assign controlled_buffer_1_out = not_1_out ? 1'b0 : 1'bz;  // Controlled_Buffer controlled_buffer_1
  not not_1 (not_1_out, and_1_out);
  assign controlled_buffer_1_out = and_1_out ? Negativo : 1'bz;  // Controlled_Buffer controlled_buffer_2
  assign controlled_buffer_3_out = and_2_out ? Overflow : 1'bz;  // Controlled_Buffer controlled_buffer_3
  not not_2 (not_2_out, and_2_out);
  assign controlled_buffer_3_out = not_2_out ? 1'b0 : 1'bz;  // Controlled_Buffer controlled_buffer_4
  or or_1 (Flag, controlled_buffer_1_out, controlled_buffer_3_out);
endmodule

module Unidade_Logica_Aritmetica__ULA (
  input  [15:0] Entrada_de_Dados,
  input  [12:0] Sinais_de_Controle,
  output [15:0] \Saída_de_Dados 
);

  wire [3:0] operacoes_1_flags;
  wire [15:0] \A_saída , \B_saída , demultiplexer_1_out0, demultiplexer_1_out1, operacoes_1_resultado,
       \registrador_de_flags_rf_1_saída , \Resultado_saída ;

  Demultiplexer #(.width(16), .tristate("true")) demultiplexer_1 (
    .out0(demultiplexer_1_out0), .out1(demultiplexer_1_out1), .in(Entrada_de_Dados),
    .sel(Sinais_de_Controle[11]), .en(Sinais_de_Controle[12]));
  Registrador_da_ULA A (
    .Entrada(demultiplexer_1_out0), .\Saída (\A_saída ),
    .Sinais_de_Controle({Sinais_de_Controle[10], Sinais_de_Controle[0]}));
  Registrador_da_ULA B (
    .Entrada(demultiplexer_1_out1), .\Saída (\B_saída ),
    .Sinais_de_Controle({Sinais_de_Controle[9], Sinais_de_Controle[0]}));
  Operacoes operacoes_1 (
    .Operando_A(\A_saída ), .Operando_B(\B_saída ), .Resultado(operacoes_1_resultado),
    .Flags(operacoes_1_flags), .Sinais_de_Controle(Sinais_de_Controle[8:5]));
  Registrador_da_ULA Resultado (
    .Entrada(operacoes_1_resultado), .\Saída (\Resultado_saída ),
    .Sinais_de_Controle({Sinais_de_Controle[2], Sinais_de_Controle[0]}));
  Registrador_de_Flags__RF registrador_de_flags_rf_1 (
    .Entrada(operacoes_1_flags), .\Saída (\registrador_de_flags_rf_1_saída ),
    .Sinais_de_Controle(Sinais_de_Controle[1:0]));
  Multiplexer #(.width(16)) multiplexer_1 (
    .in0(\Resultado_saída ), .in1(\registrador_de_flags_rf_1_saída ), .out(\Saída_de_Dados ),
    .sel(Sinais_de_Controle[3]), .en(Sinais_de_Controle[4]));

  // Other names for the same wires on the sheet: Reg__Out = Sinais_de_Controle[2]; Clock = Sinais_de_Controle[0];
  //   Reg__Flags = Sinais_de_Controle[1]; ULA_Out[1:0] = Sinais_de_Controle[4:3];
  //   Operação[3:0] = Sinais_de_Controle[8:5]; Reg__Op__B = Sinais_de_Controle[9];
  //   Reg__Op__A = Sinais_de_Controle[10]; ULA_In[1:0] = Sinais_de_Controle[12:11]

  // Notes on the sheet:
  //   Bit         Função
  //   12            Habilitar entrada da ULA
  //   11            Seleção do Registrador: 1-B; 0-A
  //   10            Controle do Registrador A
  //   9              Controle do Registrador B
  //   5,6,7,8      Seleção da Operação
  //   4              Habilitar saída da ULA
  //   3              Seleção do Registrador: 1-RR; 0-RF
  //    2             Controle do Registrador de Resultado
  //    1             Controle do Registrador de Flags
  //    0             Clock do Circuito
  //   Operações
  //   Bit         Função
  //   0000       Soma
  //   0001       Subtração
  //   0010       Multiplicação
  //   0011       Divisão
  //   0100       AND
  //   0101       OR
  //   0110       XOR
  //   0111       CMP
  //   1000        NOT
endmodule

module Memoria (
  input  [15:0] Entrada_de__Dados,
  input  [15:0] \Endereço ,
  input  [2:0] Sinais_de_Controle,
  output [15:0] \Saída_de_Dados 
);

  wire \Habilitar_Endereço , Habilitar_RAM, Habilitar_ROM, \Limpar_Completamente_a_Memória_out , not_1_out,
       Read, Write;
  wire [15:0] controlled_buffer_1_out, rom_1_data;

  and and_1 (Write, Sinais_de_Controle[2], Sinais_de_Controle[1], Sinais_de_Controle[0]);
  and and_2 (Read, Sinais_de_Controle[2], ~Sinais_de_Controle[1]);  // AND_Gate
  and and_3 (\Habilitar_Endereço , Sinais_de_Controle[2], Sinais_de_Controle[0]);
  Seletor_de_Memorias seletor_de_memorias_1 (
    .\Endereço (controlled_buffer_1_out), .Habilitar_RAM(Habilitar_RAM), .Habilitar_ROM(Habilitar_ROM));
  assign controlled_buffer_1_out = \Habilitar_Endereço  ? \Endereço  : 16'bz;  // Controlled_Buffer controlled_buffer_1
  ROM #(.addrWidth(9), .dataWidth(16)) rom_1 (
    .addr(controlled_buffer_1_out[8:0]), .data(rom_1_data), .sel(Habilitar_ROM));
  RAM #(.addrWidth(16), .dataWidth(16), .bus("asynch")) ram_1 (
    .addr(controlled_buffer_1_out), .data(rom_1_data), .sel(Habilitar_RAM), .ld(not_1_out),
    .clr(\Limpar_Completamente_a_Memória_out ));
  not not_1 (not_1_out, Sinais_de_Controle[1]);
  Button \Limpar_Completamente_a_Memória  (.out(\Limpar_Completamente_a_Memória_out ));
  assign rom_1_data = Write ? Entrada_de__Dados : 16'bz;  // Controlled_Buffer controlled_buffer_2
  assign \Saída_de_Dados  = Read ? rom_1_data : 16'bz;  // Controlled_Buffer controlled_buffer_3

  // Other names for the same wires on the sheet: Clock = Sinais_de_Controle[0]; Modo = Sinais_de_Controle[1];
  //   Habilitar = Sinais_de_Controle[2]

  // Notes on the sheet:
  //   contents of rom_1 (hex, n*v repeats v):
  //   1 fffc 5 2 fffd 10 3 fffc fffd ffff 6*0 9
endmodule

module Seletor_de_Memorias (
  input  [15:0] \Endereço ,
  output Habilitar_RAM,
  output Habilitar_ROM
);

  wire comparator_1_eq, comparator_1_lt;

  // Probe on 16'h200
  Comparator #(.width(16)) comparator_1 (
    .a(\Endereço ), .b(16'h200), .gt(Habilitar_RAM), .eq(comparator_1_eq), .lt(comparator_1_lt));
  or or_1 (Habilitar_ROM, comparator_1_eq, comparator_1_lt);
endmodule

module Unidade_de_Execucao (
  input  [15:0] \Instrução_Decodificada ,
  input  [2:0] Sinais_de_Controle,
  output [14:0] \Sinais_da_Interconexão ,
  output \Em_execução ,
  output [16:0] Sinais_da_Unidade_de_Controle,
  output [1:0] Sinais_do_Barramento
);

  wire [15:0] \contador_de_programa_pc_1_saída ;

  Contador_de_Programa__PC contador_de_programa_pc_1 (
    .Entrada(\Instrução_Decodificada ), .\Saída (\contador_de_programa_pc_1_saída ),
    .Sinais_de_Controle(Sinais_de_Controle));
  ROM #(.addrWidth(16), .dataWidth(15)) rom_1 (
    .addr(\contador_de_programa_pc_1_saída ), .data(\Sinais_da_Interconexão ), .sel(1'b1));
  ROM #(.addrWidth(16), .dataWidth(18)) rom_2 (
    .addr(\contador_de_programa_pc_1_saída ), .data({\Em_execução , Sinais_da_Unidade_de_Controle}),
    .sel(1'b1));
  ROM #(.addrWidth(16), .dataWidth(2)) rom_3 (
    .addr(\contador_de_programa_pc_1_saída ), .data(Sinais_do_Barramento), .sel(1'b1));

  // Notes on the sheet:
  //   Banco de Sinais da Interconexão
  //   Banco de Sinais da Unidade de Controle
  //   Banco de Sinais do Barramento
  //   contents of rom_1 (hex, n*v repeats v):
  //   22*0 6000 17*0 6000 13*0 5a00 0 5d00 4003 0 6008
  //   contents of rom_2 (hex, n*v repeats v):
  //   0 20000 30000 8000 8000 11*0 20080 24000 20080 21000 20400 22100 20800 20300 20080 7*0 20080 24000
  //   20080 21000 20400 20900 21000 22100 20800 20300 20080 5*0 20080 24000 20080 21000 20400 22100 20000
  //   20900 20000 20000 22100 20000 20300 20080
  //   contents of rom_3 (hex, n*v repeats v):
  //   0 2 2 14*0 2 0 2 13*0 2 0 2 0 0 2 10*0 2 0 2
endmodule

module Unidade_de_Decodificacao (
  input  [15:0] \Instrução ,
  input  Habilitar,
  output Halt,
  output [15:0] \Instrução_Decodificada 
);

  wire not_1_out;
  wire [15:0] controlled_buffer_1_out, rom_1_data;

  assign controlled_buffer_1_out = Habilitar ? \Instrução  : 16'bz;  // Controlled_Buffer controlled_buffer_1
  assign \Instrução_Decodificada  = not_1_out ? {16{1'b0}} : 16'bz;  // Controlled_Buffer controlled_buffer_2
  not not_1 (not_1_out, Habilitar);
  assign \Instrução_Decodificada  = Habilitar ? rom_1_data : 16'bz;  // Controlled_Buffer controlled_buffer_3
  ROM #(.addrWidth(16), .dataWidth(16)) rom_1 (.addr(controlled_buffer_1_out), .data(rom_1_data), .sel(Habilitar));
  and and_1 (Halt, \Instrução_Decodificada [15], \Instrução_Decodificada [14], \Instrução_Decodificada [13], \Instrução_Decodificada [12], \Instrução_Decodificada [11], \Instrução_Decodificada [10], \Instrução_Decodificada [9], \Instrução_Decodificada [8], \Instrução_Decodificada [6], \Instrução_Decodificada [5], \Instrução_Decodificada [4], \Instrução_Decodificada [3], \Instrução_Decodificada [2], \Instrução_Decodificada [1], \Instrução_Decodificada [0], \Instrução_Decodificada [7]);

  // Notes on the sheet:
  //   contents of rom_1 (hex, n*v repeats v):
  //   0 10 20 30 65531*0 ffff
endmodule

module Unidade_de_Sequencimento_e_Controle (
  input  \Sinal_da_Execução ,
  input  Sinal_de_Halt,
  output [2:0] \Controle_da_Execução ,
  output \Habilitar_Decodificação ,
  output Clok_plus,
  output Clock_minus
);

  wire clock_1_out, not_1_out, not_2_out;
  wire [2:0] counter_1_q;

  not not_1 (not_1_out, \Sinal_da_Execução );
  not not_2 (not_2_out, Sinal_de_Halt);
  Clock clock_1 (.out(clock_1_out));
  Counter #(.width(3), .max('h5)) counter_1 (
    .load(1'b0), .count(not_1_out), .Q(counter_1_q), .clk(Clok_plus), .clr(1'b0));  // open: D, carry
  assign Clok_plus = not_2_out ? clock_1_out : 1'bz;  // Controlled_Buffer controlled_buffer_1
  not not_3 (Clock_minus, Clok_plus);
  ROM #(.addrWidth(3), .dataWidth(3)) rom_1 (
    .addr(counter_1_q), .data({\Habilitar_Decodificação , \Controle_da_Execução [2:1]}), .sel(1'b1));

  assign \Controle_da_Execução [0] = Clok_plus;

  // Notes on the sheet:
  //   contents of rom_1 (hex, n*v repeats v):
  //   3 1 1 6 1 1
endmodule

module Unidade_de_Controle (
  input  [15:0] \Entrada_da_Interconexão ,
  input  [15:0] Entrada_de_Dados_do_Barramento,
  output [15:0] \Endereço_para_a_Interconexão ,
  output [15:0] \Saída_para_Interconexão ,
  output [15:0] Sinais_de_Controle_da_ULA_e_BR,
  output [2:0] Sinais_de_Controle_do_Barramento,
  output [15:0] \Endereço_para_o_Barramento ,
  output [15:0] \Saída_de_Dados_para_Barramento 
);

  wire and_1_out, and_2_out, unidade_de_decodificacao_1_halt, \unidade_de_execucao_1_em_execução ,
       \unidade_de_sequencimento_e_controle_1_habilitar_decodificação ;
  wire [1:0] unidade_de_execucao_1_sinais_da_unidade_de_controle,
       unidade_de_execucao_1_sinais_da_unidade_de_controle_2,
       unidade_de_execucao_1_sinais_da_unidade_de_controle_3,
       unidade_de_execucao_1_sinais_da_unidade_de_controle_4;
  wire [2:0] \unidade_de_sequencimento_e_controle_1_controle_da_execução ;
  wire [6:0] unidade_de_execucao_1_sinais_da_unidade_de_controle_6;
  wire [7:7] unidade_de_sequencimento_e_controle_1_clock_minus;
  wire [15:0] \RI_saída , \unidade_de_decodificacao_1_instrução_decodificada ;
  wire [16:15] unidade_de_execucao_1_sinais_da_unidade_de_controle_5;

  Registrador RI (
    .Entrada(\RI_saída ), .\Saída (\RI_saída ),
    .Sinais_de_Controle({unidade_de_execucao_1_sinais_da_unidade_de_controle_5, unidade_de_sequencimento_e_controle_1_clock_minus[7]}));
  Registrador ROP1 (
    .Entrada(\RI_saída ), .\Saída (\RI_saída ),
    .Sinais_de_Controle({unidade_de_execucao_1_sinais_da_unidade_de_controle_4, unidade_de_sequencimento_e_controle_1_clock_minus[7]}));
  Unidade_de_Deslocamento unidade_de_deslocamento_1 (
    .Entrada(\RI_saída ), .\Saída (\RI_saída ),
    .Sinais_de_Controle({unidade_de_sequencimento_e_controle_1_clock_minus[7], unidade_de_execucao_1_sinais_da_unidade_de_controle_6}));
  Registrador ROP2 (
    .Entrada(\RI_saída ), .\Saída (\RI_saída ),
    .Sinais_de_Controle({unidade_de_execucao_1_sinais_da_unidade_de_controle_3, unidade_de_sequencimento_e_controle_1_clock_minus[7]}));
  Registrador RE (
    .Entrada(\Endereço_para_a_Interconexão ), .\Saída (\RI_saída ),
    .Sinais_de_Controle({unidade_de_execucao_1_sinais_da_unidade_de_controle_2, unidade_de_sequencimento_e_controle_1_clock_minus[7]}));
  Unidade_de_Decodificacao unidade_de_decodificacao_1 (
    .\Instrução (\RI_saída ), .\Instrução_Decodificada (\unidade_de_decodificacao_1_instrução_decodificada ),
    .Halt(unidade_de_decodificacao_1_halt),
    .Habilitar(\unidade_de_sequencimento_e_controle_1_habilitar_decodificação ));
  Contador_de_Programa__PC contador_de_programa_pc_1 (
    .Entrada(\RI_saída ), .\Saída (\Endereço_para_a_Interconexão ),
    .Sinais_de_Controle({unidade_de_execucao_1_sinais_da_unidade_de_controle, unidade_de_sequencimento_e_controle_1_clock_minus[7]}));
  // Probe on \Endereço_para_a_Interconexão 
  Unidade_de_Sequencimento_e_Controle unidade_de_sequencimento_e_controle_1 (
    .\Sinal_da_Execução (\unidade_de_execucao_1_em_execução ),
    .Sinal_de_Halt(unidade_de_decodificacao_1_halt),
    .\Controle_da_Execução (\unidade_de_sequencimento_e_controle_1_controle_da_execução ),
    .\Habilitar_Decodificação (\unidade_de_sequencimento_e_controle_1_habilitar_decodificação ),
    .Clok_plus(Sinais_de_Controle_da_ULA_e_BR[0]),
    .Clock_minus(unidade_de_sequencimento_e_controle_1_clock_minus[7]));
  Direcionador direcionador_1 (
    .Entrada_A(\RI_saída ), .\Saída_B (\RI_saída ), .\Saída_A (\Saída_de_Dados_para_Barramento ),
    .Direcionador(and_2_out), .Entrada_B(Entrada_de_Dados_do_Barramento));
  // Probe on \RI_saída 
  Unidade_de_Execucao unidade_de_execucao_1 (
    .\Instrução_Decodificada (\unidade_de_decodificacao_1_instrução_decodificada ),
    .\Sinais_da_Interconexão (Sinais_de_Controle_da_ULA_e_BR[15:1]),
    .\Em_execução (\unidade_de_execucao_1_em_execução ),
    .Sinais_da_Unidade_de_Controle({unidade_de_execucao_1_sinais_da_unidade_de_controle_5, unidade_de_execucao_1_sinais_da_unidade_de_controle_4, unidade_de_execucao_1_sinais_da_unidade_de_controle_3, unidade_de_execucao_1_sinais_da_unidade_de_controle_2, unidade_de_execucao_1_sinais_da_unidade_de_controle, unidade_de_execucao_1_sinais_da_unidade_de_controle_6}),
    .Sinais_do_Barramento(Sinais_de_Controle_do_Barramento[2:1]),
    .Sinais_de_Controle(\unidade_de_sequencimento_e_controle_1_controle_da_execução ));
  Direcionador direcionador_2 (
    .Entrada_A(\Entrada_da_Interconexão ), .\Saída_B (\Saída_para_Interconexão ), .\Saída_A (\RI_saída ),
    .Direcionador(and_1_out), .Entrada_B(\RI_saída ));
  and and_1 (and_1_out, Sinais_de_Controle_da_ULA_e_BR[14], Sinais_de_Controle_da_ULA_e_BR[15]);
  and and_2 (and_2_out, ~Sinais_de_Controle_do_Barramento[1], Sinais_de_Controle_do_Barramento[2]);  // AND_Gate

  assign \Endereço_para_o_Barramento  = \Endereço_para_a_Interconexão ;
  assign Sinais_de_Controle_do_Barramento[0] = Sinais_de_Controle_da_ULA_e_BR[0];
endmodule

module Unidade_Central_de_Processamento__CPU (
  input  [15:0] Entrada_de_Dados,
  output [15:0] \Endereço ,
  output [15:0] \Saída_de_Dados ,
  output [2:0] Sinais_de_Controle_do_Barramento
);

  wire [3:1] unidade_de_controle_1_sinais_de_controle_da_ula_e_br_2;
  wire [12:0] unidade_de_controle_1_sinais_de_controle_da_ula_e_br;
  wire [15:0] \unidade_de_controle_1_endereço_para_a_interconexão ,
       \unidade_logica_aritmetica_ula_1_saída_de_dados ;

  Unidade_Logica_Aritmetica__ULA unidade_logica_aritmetica_ula_1 (
    .Entrada_de_Dados(\unidade_logica_aritmetica_ula_1_saída_de_dados ),
    .Sinais_de_Controle(unidade_de_controle_1_sinais_de_controle_da_ula_e_br),
    .\Saída_de_Dados (\unidade_logica_aritmetica_ula_1_saída_de_dados ));
  Banco_de_Registradores banco_de_registradores_1 (
    .Entrada_de_Dados(\unidade_logica_aritmetica_ula_1_saída_de_dados ),
    .\Saiída (\unidade_logica_aritmetica_ula_1_saída_de_dados ),
    .Sinais_de_Controle({unidade_de_controle_1_sinais_de_controle_da_ula_e_br_2, unidade_de_controle_1_sinais_de_controle_da_ula_e_br[0]}),
    .\Endereço (\unidade_de_controle_1_endereço_para_a_interconexão ));
  Unidade_de_Controle unidade_de_controle_1 (
    .\Endereço_para_a_Interconexão (\unidade_de_controle_1_endereço_para_a_interconexão ),
    .\Saída_para_Interconexão (\unidade_logica_aritmetica_ula_1_saída_de_dados ),
    .\Entrada_da_Interconexão (\unidade_logica_aritmetica_ula_1_saída_de_dados ),
    .Sinais_de_Controle_da_ULA_e_BR({unidade_de_controle_1_sinais_de_controle_da_ula_e_br_2, unidade_de_controle_1_sinais_de_controle_da_ula_e_br}),
    .\Endereço_para_o_Barramento (\Endereço ), .Entrada_de_Dados_do_Barramento(Entrada_de_Dados),
    .\Saída_de_Dados_para_Barramento (\Saída_de_Dados ),
    .Sinais_de_Controle_do_Barramento(Sinais_de_Controle_do_Barramento));
  // Probe on {unidade_de_controle_1_sinais_de_controle_da_ula_e_br_2, unidade_de_controle_1_sinais_de_controle_da_ula_e_br}
  // Probe on \unidade_logica_aritmetica_ula_1_saída_de_dados 
endmodule

module Barramento_Principal (
);

  wire [2:0] unidade_central_de_processamento_cpu_1_sinais_de_controle_do_barramento;
  wire [15:0] \unidade_central_de_processamento_cpu_1_endereço ,
       \unidade_central_de_processamento_cpu_1_saída_de_dados ;

  // Probe on \unidade_central_de_processamento_cpu_1_endereço 
  // Probe on \unidade_central_de_processamento_cpu_1_saída_de_dados 
  // Probe on unidade_central_de_processamento_cpu_1_sinais_de_controle_do_barramento
  Unidade_Central_de_Processamento__CPU unidade_central_de_processamento_cpu_1 (
    .Sinais_de_Controle_do_Barramento(unidade_central_de_processamento_cpu_1_sinais_de_controle_do_barramento),
    .\Endereço (\unidade_central_de_processamento_cpu_1_endereço ),
    .Entrada_de_Dados(\unidade_central_de_processamento_cpu_1_saída_de_dados ),
    .\Saída_de_Dados (\unidade_central_de_processamento_cpu_1_saída_de_dados ));
  Memoria memoria_1 (
    .\Endereço (\unidade_central_de_processamento_cpu_1_endereço ),
    .Entrada_de__Dados(\unidade_central_de_processamento_cpu_1_saída_de_dados ),
    .\Saída_de_Dados (\unidade_central_de_processamento_cpu_1_saída_de_dados ),
    .Sinais_de_Controle(unidade_central_de_processamento_cpu_1_sinais_de_controle_do_barramento));
endmodule
